// Digital circuit main.dig as structural Verilog
module main (
  input  clk,
  input  reset,
  input  [7:0] kb_data,
  input  [12:0] disp_read,
  input  kb_en,
  output [31:0] WB_MUX,
  output [31:0] DISP
);

  wire BANK_SEL, csr_flags, ctrl_bank_en, ctrl_branch_en, ctrl_csel, ctrl_enc, ctrl_flags_we, ctrl_jump_type,
       ctrl_lut_A, ctrl_lut_B, ctrl_mem_rd, ctrl_mem_wr, ctrl_mul_div_en, ctrl_pc_link_WE, ctrl_reg_we,
       HALT_IN, IR_ADDR, ir_addr_a, ir_addr_b, ir_addr_w, ir_offset, mem_rd_out, nflag_A_zero, pc_link,
       pc_out, pc_save, reg_b, reg_c, seq_exec, seq_fetch;
  wire [1:0] ctrl_cycles, ctrl_shift_op, ctrl_sp_out;
  wire [2:0] ctrl_bus_sel, ctrl_pc_cond, ctrl_pc_src, ctrl_wb_sel;
  wire [3:0] ctrl_byte_sel, ctrl_ir_sel;
  wire [11:0] ir_opcode;
  wire [15:0] mul_nxt_enc;
  wire [23:0] mem_addr, sp_out;
  wire [31:0] alu_out, ir_bus, mem_din, mem_ram_out, reg_a, shift_mul_p_enc;

  // alu_control alu_control_1: pin names not known; wires that end beside it: ir_opcode, ctrl_lut_A, ctrl_csel, ctrl_flags_we, ctrl_lut_B, ctrl_shift_op, ctrl_mul_div_en, ctrl_enc
  ir_reg_control ir_reg_control_1 (
    .op(ir_opcode), .ir_imm_sel(ctrl_ir_sel), .wb_sel(ctrl_wb_sel), .reg_we(ctrl_reg_we));
  mem_bus_control mem_bus_control_1 (.op(ir_opcode[9:0]), .ctrl_bussel(ctrl_bus_sel));
  mem_io_control mem_io_control_1 (
    .op(ir_opcode[9:0]), .bank_en(ctrl_bank_en), .mem_rd(ctrl_mem_rd), .mem_wr(ctrl_mem_wr),
    .byte_sel(ctrl_byte_sel));
  pc_control pc_control_1 (
    .op(ir_opcode[9:0]), .exec(seq_exec), .branch_en(ctrl_branch_en), .jump_type(ctrl_jump_type),
    .pc_src(ctrl_pc_src), .pc_link_we(ctrl_pc_link_WE), .cycles(ctrl_cycles), .pc_cond(ctrl_pc_cond),
    .sp_out(ctrl_sp_out), .HALT_IN(HALT_IN));
  // alu_32b_final alu_32b_final_1: pin names not known; wires that end beside it: ctrl_lut_A, ctrl_lut_B, reg_a, ir_bus, reg_c, ctrl_csel, ctrl_flags_we, clk, alu_out, csr_flags
  // register register_1: pin names not known; wires that end beside it: ctrl_reg_we, WB_MUX, ir_addr_a, ir_addr_b, ir_addr_w, seq_exec, clk, BANK_SEL, ctrl_bank_en, reg_a, reg_b, reg_c
  mul_div mul_div_1 (
    .B(ir_bus), .mode(ctrl_shift_op), .mul_div(ctrl_mul_div_en), .A(reg_a), .p_enc(ctrl_enc),
    .Out(shift_mul_p_enc), .nflag_A_is_Z(nflag_A_zero), .mul_nxt_enc(mul_nxt_enc));
  vga vga_1 (.mem_addr(mem_addr), .mem_din(WB_MUX), .disp_read_addr(disp_read), .clk(clk), .disp_data_out(DISP));
  // ir ir_1: pin names not known; wires that end beside it: mem_din, seq_fetch, clk, ctrl_ir_sel, reg_b, ir_opcode, ir_addr_a, ir_addr_b, ir_addr_w, IR_ADDR, ir_offset, ir_bus, BANK_SEL
  RAMDualPort #(.AddrBits(24), .Bits(32)) ramdualport_1 (
    .A(mem_addr), .Din(WB_MUX), .str(ctrl_mem_wr), .C(clk), .ld(mem_rd_out), .D(mem_ram_out));
  byte_lane_decoder byte_lane_decoder_1 (
    .mem_in(mem_ram_out), .sel_in(ctrl_byte_sel), .io_data_in(kb_data), .mem_out(mem_din));
  // program_counter program_counter_1: pin names not known; wires that end beside it: mem_din, alu_out, ctrl_pc_src, ir_offset, reset, ctrl_cycles, csr_flags, ctrl_pc_cond, ctrl_jump_type, ctrl_branch_en, 1'b1, HALT_IN, kb_en, 1'b1, 1'b1, 1'b1, ctrl_pc_link_WE, clk, pc_out, pc_save, seq_fetch, seq_exec, pc_link
  sp sp_1 (.sp_op(ctrl_sp_out), .CLK(clk), .Reset(reset), .sp_load_in(alu_out), .seq_exec(seq_exec), .sp_out(sp_out));
  // wb_mux wb_mux_1: pin names not known; wires that end beside it: ctrl_wb_sel, alu_out, shift_mul_p_enc, pc_save, mem_din, reg_a, ir_bus, csr_flags, mul_nxt_enc, WB_MUX
  // bus_arbitration bus_arbitration_1: pin names not known; wires that end beside it: seq_fetch, IR_ADDR, ctrl_mem_rd, ctrl_bus_sel, reg_b, pc_out, sp_out, alu_out, mem_addr, mem_rd_out
  // Pins of 10 and 12 bits meet at ir_opcode

  // Other names for the same wires on the sheet: disp_out[31:0] = DISP; disp_read_addr[12:0] = disp_read;
  //   wb_data[31:0] = WB_MUX

  // Notes on the sheet:
  //   Control Unit
  //   ALU
  //   Shift - Encoder
  //   Memory
  //   Instruction Register
  //   Program Counter
  //   Data Bus Switch
endmodule
